# Fritzing sketch HW_BombaDagua (saved by Fritzing 0.9.0b)
breadboards: 1

parts:
  Componente1 = Arduino Uno (Rev3)
  Q1 = NPN-Transistor [part_number=BC546 package="TO92 [THT]"]
  Q2 = NPN-Transistor [part_number=BC546 package="TO92 [THT]"]
  R1 = Resistor [tolerance=±5% resistance=100 package=THT]
  Q3 = NPN-Transistor [part_number=BC546 package="TO92 [THT]"]
  Q4 = NPN-Transistor [part_number=BC546 package="TO92 [THT]"]
  R2 = Resistor [tolerance=±5% resistance=100 package=THT]
  R3 = Resistor [tolerance=±5% resistance=2.2k package=THT]
  R4 = Resistor [tolerance=±5% resistance=2M package=THT]
  R5 = Resistor [tolerance=±5% resistance=2.2k package=THT]
  R6 = Resistor [tolerance=±5% resistance=2M package=THT]
  J1 = Piezo Speaker [part_number=Buzzer]
  R7 = Resistor [tolerance=±5% resistance=220 package=THT]
  Q5 = NPN-Transistor [part_number=BC546 package="TO92 [THT]"]
  D1 = Rectifier Diode [part_number=1N4001 package="300 mil [THT]"]
  U1 = RELAY [part_number="Rele 5V/10A" package=relay-g5q]
  VCC1 = Battery block 9V
  M1 = DC Motor

nets:
  D8: Componente1.D8, R7.Pin_1
  D2: Componente1.D2, Q3.C, R4.Pin_1
  D3: Componente1.D3_PWM, Q4.C, R6.Pin_1
  D4: Componente1.D4, J1.pin2
  5V/Sensor +5V: Componente1.5V, Q3.E, Q4.E, R3.Pin_1, R5.Pin_1, D1.cathode, U1.COIL2
  GND: Componente1.GND, R4.Pin_0, R6.Pin_0, J1.pin1, Q5.C, VCC1.-, M1.pin_2
  N1: Q1.E, R5.Pin_0
  N2: Q1.B, R1.Pin_0
  N3: Q1.C, Q4.B
  N4: Q2.E, R3.Pin_0
  N5: Q2.B, R2.Pin_0
  N6: Q2.C, Q3.B
  Sensor Resevatorio: R1.Pin_1
  Sensor Cisterna: R2.Pin_1
  N7: R7.Pin_0, Q5.B
  N8: Q5.E, D1.anode, U1.COIL1
  N9: U1.MAIN, VCC1.+
  N10: U1.NO, M1.pin_1

notes:
  DevidaaSuaIdeia, Controle de Bomba d'agua , 1.0
